// Logisim project Task_2.circ as structural Verilog: 1 circuit, main circuit main
module main (
  input  in_1,
  input  in_2,
  input  in_3,
  input  in_4,
  input  in_5,
  input  in_6
);

  wire and_1_out, and_2_out, or_1_out, or_2_out;

  and and_1 (and_1_out, in_1, in_3);
  and and_2 (and_2_out, and_1_out, in_5);
  or or_1 (or_1_out, in_2, in_4);
  or or_2 (or_2_out, or_1_out, in_6);
endmodule
